// Logisim project riscvpro.circ as structural Verilog: 10 circuits, main circuit RISCV
module RISCV (
);

  wire clock_1_out, comparator_black_box_1_p4, controller_1_ba, controller_1_is_i, controller_1_is_il,
       controller_1_is_s, controller_1_is_u, controller_1_slt, controller_1_we, id2sel_1_p3, or_1_out,
       or_2_out, ram_1_p6;
  wire [1:0] ba2wa_1_id;
  wire [2:0] controller_1_ft3;
  wire [3:0] aluopparser_1_op;
  wire [4:0] alu_1_p4, controller_1_xa, controller_1_xb, controller_1_xw;
  wire [6:0] controller_1_ft7;
  wire [19:0] ba2wa_1_wa;
  wire [31:0] alu_1_p5, ba2wa_1_dataout, bit_extender_1_out, controller_1_imm, ic4_1_pc4, multiplexer_1_out,
       multiplexer_2_out, multiplexer_3_out, ram_1_p7, ramoutputfmt_1_dout, register_1_q, registerfile_1_p1,
       registerfile_1_p6, registerfile_1_p7, risc_vprogramrom_1_p2;

  Clock clock_1 (.out(clock_1_out));
  Register #(.width(32)) register_1 (.D(ic4_1_pc4), .clk(clock_1_out), .Q(register_1_q));  // open: en, clr
  IC4 ic4_1 (.PC(register_1_q), .PC4(ic4_1_pc4));
  // RISC_VProgramROM risc_vprogramrom_1: pin names not known; wires that end beside it: register_1_q, risc_vprogramrom_1_p2, clock_1_out
  Controller controller_1 (
    .Cmd(risc_vprogramrom_1_p2), .WE(controller_1_we), .xW(controller_1_xw), .xA(controller_1_xa),
    .xB(controller_1_xb), .is_S(controller_1_is_s), .is_I(controller_1_is_i), .is_IL(controller_1_is_il),
    .is_U(controller_1_is_u), .imm(controller_1_imm), .FT3(controller_1_ft3), .FT7(controller_1_ft7),
    .BA(controller_1_ba), .SLT(controller_1_slt));
  // RegisterFile registerfile_1: pin names not known; wires that end beside it: registerfile_1_p1, controller_1_we, controller_1_xw, controller_1_xa, controller_1_xb, registerfile_1_p6, registerfile_1_p7
  or or_1 (or_1_out, controller_1_is_s, controller_1_is_i);
  or or_2 (or_2_out, controller_1_is_s, controller_1_is_il);
  Multiplexer #(.width(32), .enable("false")) multiplexer_1 (
    .in0(registerfile_1_p7), .in1(controller_1_imm), .out(multiplexer_1_out), .sel(or_1_out));
  Multiplexer #(.width(32), .enable("false")) multiplexer_2 (
    .in0(registerfile_1_p6), .in1(controller_1_imm), .out(multiplexer_2_out), .sel(controller_1_is_u));
  AluOpParser aluopparser_1 (
    .FT3(controller_1_ft3), .FT7(controller_1_ft7), .LUI(controller_1_is_u), .MemAdd(or_2_out),
    .Op(aluopparser_1_op));
  // Comparator_Black_Box comparator_black_box_1: pin names not known; wires that end beside it: registerfile_1_p6, registerfile_1_p7, controller_1_slt, comparator_black_box_1_p4
  // ALU alu_1: pin names not known; wires that end beside it: multiplexer_2_out, multiplexer_1_out, aluopparser_1_op, alu_1_p4, alu_1_p5
  SA sa_1 (.B(registerfile_1_p7), .LUI(controller_1_is_u), .Sa(alu_1_p4));
  assign bit_extender_1_out = {{31{1'b0}}, comparator_black_box_1_p4};  // Bit_Extender bit_extender_1
  Multiplexer #(.width(32), .enable("false")) multiplexer_3 (
    .in0(alu_1_p5), .in1(bit_extender_1_out), .out(multiplexer_3_out), .sel(controller_1_slt));
  Ba2Wa ba2wa_1 (
    .Add(multiplexer_3_out), .DataIn(registerfile_1_p7), .BA(controller_1_ba), .WA(ba2wa_1_wa),
    .DataOut(ba2wa_1_dataout), .Id(ba2wa_1_id));
  // Id2Sel id2sel_1: pin names not known; wires that end beside it: controller_1_ba, ba2wa_1_id, id2sel_1_p3, ba2wa_1_dataout
  RamOutputFmt ramoutputfmt_1 (.Data(ram_1_p7), .Id(ba2wa_1_id), .BA(controller_1_ba), .DOut(ramoutputfmt_1_dout));
  // RAM ram_1: pin names not known; wires that end beside it: ba2wa_1_wa, ba2wa_1_dataout, controller_1_is_s, id2sel_1_p3, clock_1_out, ram_1_p6, ram_1_p7
  not not_1 (ram_1_p6, controller_1_is_s);
  Multiplexer #(.width(32), .enable("false")) multiplexer_4 (
    .in0(multiplexer_3_out), .in1(ramoutputfmt_1_dout), .out(registerfile_1_p1), .sel(controller_1_is_il));

  // Notes on the sheet:
  //   contents of risc_vprogramrom_1 (hex, n*v repeats v):
  //   addi x1, x0, 0x123 addi x2, x0, 3 sll x1, x1, x2 addi x2, x2, -1 sra x1, x1, x2 lui x1, 2048 lui x2,
  //   255 add x1, x1, x2 sw x1, 0(x0) sb x1, 1(x0) lb x3, 2(x0) lw x4, 0(x0) addi x5, x0, 16 sra x4, x4,
  //   x5 sra x4, x3, x5 sub x4, x3, x4 and x5, x1, x4 andi x5, x5, 0x7ff xor x5, x1, x1 sw x1, 5(x0) xori
  //   x5, x5, 0x561 xori x5, x5, -1 slt x6, x1, x3 slt x7, x2, x1 slt x8, x4, x2 slti x9, x3, 0 addi x10,
  //   x0, 4 sll x7, x7, x10 or x10, x8, x7 ori x10, x10, 0x300
endmodule

module IC4 (
  input  [31:0] PC,
  output [31:0] PC4
);

  // Incrementer #(.width(30)) incrementer_1: pin names not known; wires that end beside it: PC[31:2], PC4[31:2]

  assign PC4[1:0] = PC[1:0];
endmodule

module Controller (
  input  [31:0] Cmd,
  output WE,
  output [4:0] xW,
  output [4:0] xA,
  output [4:0] xB,
  output is_S,
  output is_I,
  output is_IL,
  output is_U,
  output [31:0] imm,
  output [2:0] FT3,
  output [6:0] FT7,
  output BA,
  output SLT
);

  wire and_1_out, and_2_out, not_2_out, not_3_out, or_1_out, or_2_out, R_type;
  wire [2:0] bit_extender_4_out;
  wire [6:0] bit_extender_3_out;
  wire [11:0] imm_12;
  wire [31:0] bit_extender_1_out, bit_extender_2_out;

  not not_1 (WE, is_S);
  Multiplexer #(.width(12), .enable("false")) multiplexer_1 (
    .in0({Cmd[31:25], Cmd[11:7]}), .in1(Cmd[31:20]), .out(imm_12), .sel(is_I));
  assign bit_extender_1_out = {{20{imm_12[11]}}, imm_12};  // Bit_Extender bit_extender_1
  assign bit_extender_2_out = {{12{1'b0}}, Cmd[31:12]};  // Bit_Extender bit_extender_2
  or or_1 (or_1_out, is_S, is_IL);
  and and_1 (and_1_out, is_I, ~is_IL);  // AND_Gate
  and and_2 (and_2_out, ~Cmd[12], Cmd[13], ~Cmd[14]);  // AND_Gate
  not not_2 (not_2_out, Cmd[2]);
  assign bit_extender_3_out = {{6{R_type}}, R_type};  // Bit_Extender bit_extender_3
  not not_3 (not_3_out, Cmd[13]);
  or or_2 (or_2_out, and_1_out, R_type);
  Multiplexer #(.width(32), .enable("false")) multiplexer_2 (
    .in0(bit_extender_1_out), .in1(bit_extender_2_out), .out(imm), .sel(Cmd[2]));
  assign bit_extender_4_out = {{2{not_2_out}}, not_2_out};  // Bit_Extender bit_extender_4
  assign FT3 = bit_extender_4_out & Cmd[14:12];  // AND_Gate and_3, 3 bits wide
  assign FT7 = Cmd[31:25] & bit_extender_3_out;  // AND_Gate and_4, 7 bits wide
  and and_5 (BA, not_3_out, or_1_out);
  and and_6 (SLT, or_2_out, and_2_out);
  and and_7 (R_type, Cmd[5], Cmd[4], ~Cmd[2]);  // AND_Gate
  not not_4 (is_I, Cmd[5]);
  nor nor_1 (is_IL, Cmd[5], Cmd[4]);
  and and_8 (is_S, Cmd[5], ~Cmd[4]);  // AND_Gate

  assign is_U = Cmd[2];
  assign xA = Cmd[19:15];
  assign xB = Cmd[24:20];
  assign xW = Cmd[11:7];

  // Other names for the same wires on the sheet: imm5[4:0] = Cmd[11:7]; rd[4:0] = Cmd[11:7]; I_type = is_I;
  //   IL_type = is_IL; funct3[2:0] = Cmd[14:12]; imm20[19:0] = Cmd[31:12]; rs1[4:0] = Cmd[19:15];
  //   imm12[11:0] = Cmd[31:20]; rs2[4:0] = Cmd[24:20]; funct7[6:0] = Cmd[31:25]; imm7[6:0] = Cmd[31:25];
  //   Opcode[6:0] = Cmd[6:0]; U_type = Cmd[2]; S_type = is_S
endmodule

module AluOpParser (
  input  [2:0] FT3,
  input  [6:0] FT7,
  input  LUI,
  input  MemAdd,
  output [3:0] Op
);

  wire [1:1] not_4_out;
  wire [2:2] or_1_out;
  wire [3:0] multiplexer_1_out;
  wire [3:1] not_2_out;
  wire [3:3] not_3_out;

  or or_1 (or_1_out[2], FT7[5], FT3[1]);
  Multiplexer #(.select(3), .width(4), .enable("false")) multiplexer_1 (
    .in0({FT3[2], or_1_out[2], {2{FT3[0]}}}), .in1({FT3, FT3[0]}), .in2({{2{FT3[1]}}, FT3[0], FT3[1]}),
    .in3({{2{FT3[1]}}, FT3[2:1]}), .in4({{2{FT3[2]}}, {2{FT3[0]}}}), .in5({FT3[1:0], {2{FT3[0]}}}),
    .in6({FT3[2:1], FT3[1:0]}), .in7({FT3, FT3[0]}), .out(multiplexer_1_out), .sel(FT3));
  not not_1 (not_2_out[3], LUI);
  not not_2 (not_2_out[1], not_2_out[3]);
  not not_3 (not_3_out[3], MemAdd);
  not not_4 (not_4_out[1], LUI);
  Multiplexer #(.select(2), .width(4), .enable("false")) multiplexer_2 (
    .in0(multiplexer_1_out), .in1({{2{not_2_out[3]}}, not_2_out[1], not_2_out[3]}), .in2({4{not_3_out[3]}}),
    .in3({{2{LUI}}, not_4_out[1], LUI}), .out(Op), .sel({MemAdd, LUI}));

  // Other names for the same wires on the sheet: FT7_t = FT7[5]
endmodule

module RamWrapper (
  input  [31:0] Add,
  input  [31:0] DataIn,
  input  WE,
  input  BA,
  input  clk,
  output [31:0] DataOut
);

  wire not_1_out, not_2_out;
  wire [3:0] bit_extender_3_out, decoder_1_out0, multiplexer_2_out;
  wire [19:0] bit_extender_1_out, bit_extender_2_out, multiplexer_1_out;

  Bit_Extender #(.in_width(32), .out_width(20)) bit_extender_1 (.in(Add), .out(bit_extender_1_out));
  Decoder #(.select(2)) decoder_1 (
    .out0(decoder_1_out0[0]), .out1(decoder_1_out0[1]), .out2(decoder_1_out0[2]), .out3(decoder_1_out0[3]),
    .sel(bit_extender_1_out[1:0]), .en(BA));
  assign bit_extender_2_out = {{2{bit_extender_1_out[19]}}, bit_extender_1_out[19:2]};  // Bit_Extender bit_extender_2
  Multiplexer #(.width(20), .enable("false")) multiplexer_1 (
    .in0(bit_extender_1_out), .in1(bit_extender_2_out), .out(multiplexer_1_out), .sel(BA));
  not not_1 (not_1_out, BA);
  assign bit_extender_3_out = {{3{not_1_out}}, not_1_out};  // Bit_Extender bit_extender_3
  Multiplexer #(.width(4), .enable("false")) multiplexer_2 (
    .in0(bit_extender_3_out), .in1(decoder_1_out0), .out(multiplexer_2_out), .sel(BA));
  not not_2 (not_2_out, WE);
  // RAM ram_1: pin names not known; wires that end beside it: multiplexer_1_out, DataIn, WE, multiplexer_2_out, clk, not_2_out, DataOut
endmodule

module SA (
  input  [31:0] B,
  input  LUI,
  output [4:0] Sa
);

  wire [4:0] not_3_out;

  not not_1 (not_3_out[4], LUI);
  not not_2 (not_3_out[1], LUI);
  not not_3 (not_3_out[0], LUI);
  Multiplexer #(.width(5), .enable("false")) multiplexer_1 (
    .in0(B[4:0]), .in1({not_3_out[4], {2{LUI}}, not_3_out[1:0]}), .out(Sa), .sel(LUI));
endmodule

module Ba2Wa (
  input  [31:0] Add,
  input  [31:0] DataIn,
  input  BA,
  output [19:0] WA,
  output [31:0] DataOut,
  output [1:0] Id
);

  assign WA = {{2{1'b0}}, Add[19:2]};  // Bit_Extender bit_extender_1
  BytePos bytepos_1 (.Id(Add[1:0]), .DataIn(DataIn), .BA(BA), .DataOut(DataOut));

  assign Id = Add[1:0];
endmodule

module RamOutputFmt (
  input  [31:0] Data,
  input  [1:0] Id,
  input  BA,
  output [31:0] DOut
);

  wire [3:0] id2sel_1_sel;
  wire [7:0] bit_extender_1_out, bit_extender_2_out, bit_extender_3_out, bit_extender_4_out,
       bitselector_1_out, multiplexer_1_out, multiplexer_2_out, multiplexer_3_out, multiplexer_4_out;
  wire [31:0] bit_extender_5_out;

  Id2Sel id2sel_1 (.Id(Id), .BA(BA), .Sel(id2sel_1_sel));
  assign bit_extender_1_out = {{7{id2sel_1_sel[0]}}, id2sel_1_sel[0]};  // Bit_Extender bit_extender_1
  assign bit_extender_2_out = {{7{id2sel_1_sel[1]}}, id2sel_1_sel[1]};  // Bit_Extender bit_extender_2
  assign bit_extender_3_out = {{7{id2sel_1_sel[2]}}, id2sel_1_sel[2]};  // Bit_Extender bit_extender_3
  assign bit_extender_4_out = {{7{id2sel_1_sel[3]}}, id2sel_1_sel[3]};  // Bit_Extender bit_extender_4
  Multiplexer #(.width(8), .enable("false")) multiplexer_1 (
    .in0(bit_extender_1_out), .in1(Data[7:0]), .out(multiplexer_1_out), .sel(id2sel_1_sel[0]));
  Multiplexer #(.width(8), .enable("false")) multiplexer_2 (
    .in0(bit_extender_2_out), .in1(Data[15:8]), .out(multiplexer_2_out), .sel(id2sel_1_sel[1]));
  Multiplexer #(.width(8), .enable("false")) multiplexer_3 (
    .in0(bit_extender_3_out), .in1(Data[23:16]), .out(multiplexer_3_out), .sel(id2sel_1_sel[2]));
  Multiplexer #(.width(8), .enable("false")) multiplexer_4 (
    .in0(bit_extender_4_out), .in1(Data[31:24]), .out(multiplexer_4_out), .sel(id2sel_1_sel[3]));
  BitSelector #(.width(32), .group(8)) bitselector_1 (
    .in({multiplexer_4_out, multiplexer_3_out, multiplexer_2_out, multiplexer_1_out}),
    .out(bitselector_1_out), .sel(Id));
  assign bit_extender_5_out = {{24{bitselector_1_out[7]}}, bitselector_1_out};  // Bit_Extender bit_extender_5
  Multiplexer #(.width(32), .enable("false")) multiplexer_5 (
    .in0({multiplexer_4_out, multiplexer_3_out, multiplexer_2_out, multiplexer_1_out}),
    .in1(bit_extender_5_out), .out(DOut), .sel(BA));
endmodule

module Id2Sel (
  input  [1:0] Id,
  input  BA,
  output [3:0] Sel
);

  wire not_1_out;
  wire [3:0] bit_extender_1_out, decoder_1_out0;

  Decoder #(.select(2)) decoder_1 (
    .out0(decoder_1_out0[0]), .out1(decoder_1_out0[1]), .out2(decoder_1_out0[2]), .out3(decoder_1_out0[3]),
    .sel(Id), .en(BA));
  not not_1 (not_1_out, BA);
  assign bit_extender_1_out = {{3{not_1_out}}, not_1_out};  // Bit_Extender bit_extender_1
  Multiplexer #(.width(4), .enable("false")) multiplexer_1 (
    .in0(bit_extender_1_out), .in1(decoder_1_out0), .out(Sel), .sel(BA));
endmodule

module BytePos (
  input  [1:0] Id,
  input  [31:0] DataIn,
  input  BA,
  output [31:0] DataOut
);

  wire decoder_1_out0, decoder_1_out1, decoder_1_out2, decoder_1_out3;
  wire [7:0] and_1_out, and_2_out, and_3_out, and_4_out, bit_extender_1_out, bit_extender_2_out,
       bit_extender_3_out, bit_extender_4_out;

  Decoder #(.select(2)) decoder_1 (
    .out0(decoder_1_out0), .out1(decoder_1_out1), .out2(decoder_1_out2), .out3(decoder_1_out3), .sel(Id),
    .en(BA));
  assign bit_extender_1_out = {{7{decoder_1_out0}}, decoder_1_out0};  // Bit_Extender bit_extender_1
  assign bit_extender_2_out = {{7{decoder_1_out1}}, decoder_1_out1};  // Bit_Extender bit_extender_2
  assign bit_extender_3_out = {{7{decoder_1_out2}}, decoder_1_out2};  // Bit_Extender bit_extender_3
  assign bit_extender_4_out = {{7{decoder_1_out3}}, decoder_1_out3};  // Bit_Extender bit_extender_4
  assign and_1_out = DataIn[7:0] & bit_extender_1_out;  // AND_Gate and_1, 8 bits wide
  assign and_2_out = DataIn[7:0] & bit_extender_2_out;  // AND_Gate and_2, 8 bits wide
  assign and_3_out = DataIn[7:0] & bit_extender_3_out;  // AND_Gate and_3, 8 bits wide
  assign and_4_out = DataIn[7:0] & bit_extender_4_out;  // AND_Gate and_4, 8 bits wide
  Multiplexer #(.width(32), .enable("false")) multiplexer_1 (
    .in0(DataIn), .in1({and_4_out, and_3_out, and_2_out, and_1_out}), .out(DataOut), .sel(BA));
endmodule
